# Fritzing sketch main_diagram (saved by Fritzing 1.0.5)
breadboards: 1

parts:
  Raspberry_Pi_4_Model_B = Raspberry Pi 4B
  HC-SR501_PIR_sensor_/_5V = HC-SR501 Body Sensor Module
  MH-Z19C1 = MH-Z19C
  Part1 = KY-037 High Sensitivity Sound Detection Module [package="Breakout board"]
  DHT22_/_3_3V = DHT22 module

nets:
  N1: Raspberry_Pi_4_Model_B.3V3, DHT22_/_3_3V.+
  5V: Raspberry_Pi_4_Model_B.5V, HC-SR501_PIR_sensor_/_5V.VCC, MH-Z19C1.Vin, Part1.+
  GND: Raspberry_Pi_4_Model_B.GND, HC-SR501_PIR_sensor_/_5V.GND, MH-Z19C1.GND, Part1.G, DHT22_/_3_3V.-
  N2: Raspberry_Pi_4_Model_B.GPIO4, DHT22_/_3_3V.Out
  N3: Raspberry_Pi_4_Model_B.GPIO14, MH-Z19C1.Rx
  N4: Raspberry_Pi_4_Model_B.GPIO15, MH-Z19C1.Tx
  N5: Raspberry_Pi_4_Model_B.GPIO17, HC-SR501_PIR_sensor_/_5V.OUT
  N6: Raspberry_Pi_4_Model_B.GPIO27, Part1.D0

notes:
  <--- 3.3 Volts
  <--- 5 Volts
  Although the connector type is different, both the pin header and wafer versions of the MH-Z19C, they share the same electrical pinout and function; only the physical layout and wire orientation differ
  For more details, refer to:
  https://www.winsen-sensor.com/d/files/mh-z19c-pins%26terminal-type-co2-manual(ver1_2).pdf

custom parts:
  HC-SR501 Body Sensor Module: Pyroelectric Infrared PIR Motion Sensor Detector Module
  MH-Z19C: CO2-Sensor https://www.winsen-sensor.com/
  KY-037 High Sensitivity Sound Detection Module: KY-037 high sensitivity sound detection module is an analog/digital sensor that uses a condenser microphone to observe changes in environment noise.
  DHT22 module: DHT22 module. Pins VCC Data GND.
